// Logisim project navrh-priprava.circ as structural Verilog: 1 circuit, main circuit 15
module _15 (
  input  DIN_0,
  input  DIN_1,
  input  DIN_2,
  input  DIN_3,
  input  DIN_RDY
);

  wire clock_1_out, comparator_1_eq, d_ff_2_q, d_ff_3_q, d_ff_4_q;
  wire [1:0] counter_1_q, counter_2_q;

  Clock clock_1 (.out(clock_1_out));
  Counter #(.width(2), .max('h3)) counter_1 (.Q(counter_1_q));  // open: load, D, count, carry, clk, clr
  D_Flip_Flop d_ff_1 (.clk(clock_1_out), .D(DIN_0), .Q(clock_1_out), .en(DIN_RDY));  // open: Qn, preset, reset
  D_Flip_Flop d_ff_2 (.clk(clock_1_out), .D(DIN_1), .Q(d_ff_2_q), .en(DIN_RDY));  // open: Qn, preset, reset
  D_Flip_Flop d_ff_3 (.clk(clock_1_out), .D(DIN_2), .Q(d_ff_3_q), .en(DIN_RDY));  // open: Qn, preset, reset
  D_Flip_Flop d_ff_4 (.clk(clock_1_out), .D(DIN_3), .Q(d_ff_4_q), .en(DIN_RDY));  // open: Qn, preset, reset
  Comparator #(.width(2)) comparator_1 (.a(2'b11), .b(counter_1_q), .eq(comparator_1_eq));  // open: gt, lt
  Counter #(.width(2), .max('h3)) counter_2 (
    .Q(counter_2_q), .clk(comparator_1_eq));  // open: load, D, count, carry, clr
  Multiplexer #(.select(2)) multiplexer_1 (
    .in0(clock_1_out), .in1(d_ff_2_q), .in2(d_ff_3_q), .in3(d_ff_4_q), .sel(counter_2_q));  // open: out, en
endmodule
