// Logisim project navrh-stream.circ as structural Verilog: 1 circuit, main circuit main
module main (
  input  DIN_0,
  input  DIN_1,
  input  DIN_2,
  input  DIN_3,
  input  DVLD,
  output DOUT
);

  wire CLK_out, comparator_1_eq, d_ff_1_q, d_ff_2_q, d_ff_3_q, d_ff_3_qn, d_ff_4_q;
  wire [1:0] counter_1_q, counter_2_q;

  Clock CLK (.out(CLK_out));
  D_Flip_Flop d_ff_1 (.clk(CLK_out), .D(DIN_0), .Q(d_ff_1_q));  // open: Qn, preset, en, reset
  D_Flip_Flop d_ff_2 (.clk(CLK_out), .D(DIN_1), .Q(d_ff_2_q));  // open: Qn, preset, en, reset
  D_Flip_Flop d_ff_3 (.clk(CLK_out), .D(DIN_2), .Q(d_ff_3_q), .Qn(d_ff_3_qn), .reset(d_ff_3_qn));  // open: preset, en
  D_Flip_Flop d_ff_4 (.clk(CLK_out), .D(DIN_3), .Q(d_ff_4_q));  // open: Qn, preset, en, reset
  Counter #(.width(2), .max('h3)) counter_1 (.Q(counter_1_q), .clk(CLK_out));  // open: load, D, count, carry, clr
  Comparator #(.width(2)) comparator_1 (.a(2'b11), .b(counter_1_q), .eq(comparator_1_eq));  // open: gt, lt
  Multiplexer #(.select(2)) multiplexer_1 (
    .in0(d_ff_1_q), .in1(d_ff_2_q), .in2(d_ff_3_q), .in3(d_ff_4_q), .out(DOUT), .sel(counter_2_q),
    .en(comparator_1_eq));
  Counter #(.width(2), .max('h3)) counter_2 (
    .Q(counter_2_q), .clk(comparator_1_eq));  // open: load, D, count, carry, clr
endmodule
